# Fritzing sketch Microsoft.IoT.Bulbs (saved by Fritzing 0.9.2b)

parts:
  LED1 = RGB LED (com. cathode, rgb) [package="5 mm [THT]"]
  Raspberry_Pi1 = Raspberry Pi 2

nets:
  N1: LED1.red_anode, Raspberry_Pi1.GND
  N2: LED1.common_cathode, Raspberry_Pi1.GPIO26
  N3: LED1.green_anode, Raspberry_Pi1.GPIO13
  N4: LED1.blue_anode, Raspberry_Pi1.GPIO6

notes:
  Red
  GND
  Green
  Blue
